// Logisim project CAN_receiver.circ as structural Verilog: 3 circuits, main circuit main
// 4
module main (
  input  data_in,
  input  in_2,
  output flag_out
);

  wire and_1_out, and_2_out, and_3_out, and_4_out, and_5_out, and_6_out, and_7_out, clk_out, d_ff_1_q,
       d_ff_2_q, d_ff_3_q, not_1_out, not_2_out, not_3_out, not_4_out, s_r_ff_1_q, shift_register_1_p4,
       t_ff_1_q, t_ff_1_qn, t_ff_2_qn, t_ff_3_qn, t_ff_4_q, t_ff_5_qn, t_ff_6_qn, t_ff_7_q;

  Clock clk (.out(clk_out));
  D_Flip_Flop d_ff_1 (.D(not_1_out), .clk(clk_out), .Q(d_ff_1_q));  // open: Qn, preset, reset
  not not_1 (not_1_out, data_in);
  and and_1 (and_1_out, data_in, and_3_out);
  not not_2 (not_2_out, and_3_out);
  D_Flip_Flop d_ff_2 (.D(and_1_out), .clk(clk_out), .Q(d_ff_2_q));  // open: Qn, preset, reset
  and and_2 (and_2_out, d_ff_1_q, not_2_out);
  D_Flip_Flop d_ff_3 (.D(d_ff_2_q), .clk(clk_out), .Q(d_ff_3_q));  // open: Qn, preset, reset
  T_Flip_Flop t_ff_1 (.T(and_2_out), .clk(clk_out), .Q(t_ff_1_q), .Qn(t_ff_1_qn), .reset(and_4_out));  // open: preset
  not not_3 (not_3_out, and_3_out);
  and and_3 (and_3_out, t_ff_4_q, t_ff_1_q);
  not not_4 (not_4_out, d_ff_2_q);
  and and_4 (and_4_out, data_in, not_3_out);
  T_Flip_Flop t_ff_2 (.T(and_2_out), .clk(t_ff_1_qn), .Qn(t_ff_2_qn), .reset(and_4_out));  // open: Q, preset
  and and_5 (and_5_out, not_4_out, d_ff_3_q);
  and and_6 (and_6_out, s_r_ff_1_q, flag_out);
  T_Flip_Flop t_ff_3 (.T(and_2_out), .clk(t_ff_2_qn), .Qn(t_ff_3_qn), .reset(and_4_out));  // open: Q, preset
  S_R_Flip_Flop s_r_ff_1 (.S(and_5_out), .R(in_2), .clk(clk_out), .Q(s_r_ff_1_q));  // open: reset, Qn, preset
  T_Flip_Flop t_ff_4 (.T(and_2_out), .clk(t_ff_3_qn), .Q(t_ff_4_q), .reset(and_4_out));  // open: Qn, preset
  and and_7 (and_7_out, s_r_ff_1_q, data_in);
  T_Flip_Flop t_ff_5 (.T(and_6_out), .clk(clk_out), .Qn(t_ff_5_qn));  // open: Q, reset, preset
  T_Flip_Flop t_ff_6 (.T(and_6_out), .clk(t_ff_5_qn), .Qn(t_ff_6_qn));  // open: Q, reset, preset
  // Shift_Register #(.length(4), .parallel("false")) shift_register_1: pin names not known; wires that end beside it: s_r_ff_1_q, flag_out, clk_out, shift_register_1_p4
  and and_8 (shift_register_1_p4, and_7_out, flag_out);
  T_Flip_Flop t_ff_7 (.T(and_6_out), .clk(t_ff_6_qn), .Q(t_ff_7_q));  // open: Qn, reset, preset
  not not_5 (flag_out, t_ff_7_q);
endmodule

module Data_storage_8_bit (
  input  in_1,
  input  in_2,
  input  in_3
);

  wire and_1_out, and_2_out, clock_1_out, main_1_flag_out, shift_register_1_p1, shift_register_1_p4,
       t_ff_1_q, t_ff_1_qn, t_ff_2_q, t_ff_2_qn, t_ff_3_q;
  wire [6:0] sipo_1_out_3;

  Clock clock_1 (.out(clock_1_out));
  and and_1 (and_1_out, main_1_flag_out, shift_register_1_p1);
  T_Flip_Flop t_ff_1 (.T(and_1_out), .clk(clock_1_out), .Q(t_ff_1_q), .Qn(t_ff_1_qn));  // open: reset, preset
  T_Flip_Flop t_ff_2 (.T(and_1_out), .clk(t_ff_1_qn), .Q(t_ff_2_q), .Qn(t_ff_2_qn));  // open: reset, preset
  main main_1 (.data_in(in_1), .in_2(clock_1_out), .flag_out(main_1_flag_out));
  and and_2 (and_2_out, in_1, shift_register_1_p1);
  T_Flip_Flop t_ff_3 (.T(and_1_out), .clk(t_ff_2_qn), .Q(t_ff_3_q));  // open: Qn, reset, preset
  // Shift_Register #(.parallel("false")) shift_register_1: pin names not known; wires that end beside it: shift_register_1_p1, clock_1_out, and_2_out, shift_register_1_p4
  nand nand_1 (shift_register_1_p1, t_ff_3_q, t_ff_2_q, t_ff_1_q);
  TTY tty_1 (.data(sipo_1_out_3), .clk(in_2), .clr(in_3));  // open: we
  SIPO sipo_1 (.in_1(shift_register_1_p4), .in_2(clock_1_out), .out_3(sipo_1_out_3));
endmodule

module SIPO (
  input  in_1,
  input  in_2,
  output [6:0] out_3
);

  wire d_ff_1_q;

  D_Flip_Flop d_ff_1 (.D(in_1), .clk(in_2), .Q(d_ff_1_q));  // open: Qn, preset, reset
  D_Flip_Flop d_ff_2 (.D(d_ff_1_q), .clk(in_2), .Q(out_3[6]));  // open: Qn, preset, reset
  D_Flip_Flop d_ff_3 (.D(out_3[6]), .clk(in_2), .Q(out_3[5]));  // open: Qn, preset, reset
  D_Flip_Flop d_ff_4 (.D(out_3[5]), .clk(in_2), .Q(out_3[4]));  // open: Qn, preset, reset
  D_Flip_Flop d_ff_5 (.D(out_3[4]), .clk(in_2), .Q(out_3[3]));  // open: Qn, preset, reset
  D_Flip_Flop d_ff_6 (.D(out_3[3]), .clk(in_2), .Q(out_3[2]));  // open: Qn, preset, reset
  D_Flip_Flop d_ff_7 (.D(out_3[2]), .clk(in_2), .Q(out_3[1]));  // open: Qn, preset, reset
  D_Flip_Flop d_ff_8 (.D(out_3[1]), .clk(in_2), .Q(out_3[0]));  // open: Qn, preset, reset
endmodule
