// Logisim project iter1.circ as structural Verilog: 1 circuit, main circuit main
module main (
  input  in_1,
  input  in_2,
  input  Reset,
  input  [2:0] in_4,
  input  Start,
  input  [7:0] in_6
);

  wire clk_out, d_ff_1_q, shift_register_1_p2, shift_register_1_p13;
  wire [2:0] counter_2_q;
  wire [7:0] counter_1_q, rom_1_data;

  D_Flip_Flop d_ff_1 (.D(1'b1), .clk(Start), .Q(d_ff_1_q), .reset(shift_register_1_p2));  // open: Qn, preset
  Counter #(.ongoal("stay")) counter_1 (
    .clr(Reset), .load(d_ff_1_q), .up(1'b0), .count(1'b1), .clk(shift_register_1_p2), .D(in_6),
    .Q(counter_1_q));  // open: carry
  Clock clk (.out(clk_out));
  ROM rom_1 (.addr(counter_1_q), .data(rom_1_data));
  // Shift_Register #(.length(7)) shift_register_1: pin names not known; wires that end beside it: in_2, shift_register_1_p2, clk_out, clk_out, rom_1_data[0], rom_1_data[1], rom_1_data[2], rom_1_data[3], rom_1_data[4], rom_1_data[5], rom_1_data[6], rom_1_data[7], shift_register_1_p13
  Counter #(.max('h7), .width(3)) counter_2 (
    .clr(in_1), .load(shift_register_1_p2), .up(1'b0), .count(1'b1), .clk(clk_out), .D(in_4), .Q(counter_2_q));  // open: carry
  // Probe on shift_register_1_p13
  nor nor_1 (shift_register_1_p2, counter_2_q[0], counter_2_q[1], counter_2_q[2]);

  // Notes on the sheet:
  //   in_6: initial=0x101
  //   contents of rom_1 (hex, n*v repeats v):
  //   11 1 ff
endmodule
