// Logisim project iter2.circ as structural Verilog: 1 circuit, main circuit main
module main (
  input  Tx1,
  input  Tx2,
  input  Tx3,
  output Rx1,
  output Rx3
);

  wire and_1_out, and_2_out, clock_1_out, d_ff_1_q, not_1_out, not_2_out, not_3_out, not_4_out, out1;
  wire [7:0] counter_1_q;

  Clock clock_1 (.out(clock_1_out));
  not not_1 (not_1_out, Rx1);
  D_Flip_Flop d_ff_1 (.D(and_1_out), .clk(and_1_out), .Q(d_ff_1_q), .reset(out1));  // open: Qn, preset
  and and_1 (and_1_out, clock_1_out, not_1_out);
  and and_2 (and_2_out, d_ff_1_q, clock_1_out);
  Counter counter_1 (.clr(out1), .up(1'b1), .count(1'b1), .clk(and_2_out), .Q(counter_1_q));  // open: load, D, carry
  and and_3 (out1, counter_1_q[3], counter_1_q[6]);
  not not_2 (not_2_out, Tx1);
  not not_3 (not_3_out, Tx2);
  not not_4 (not_4_out, Tx3);
  // Transmission_Gate transmission_1: pin names not known; wires that end beside it: 1'b0, Tx1, not_2_out, Rx1
  // Transmission_Gate transmission_2: pin names not known; wires that end beside it: 1'b0, Tx2, not_3_out, Rx1
  // Transmission_Gate transmission_3: pin names not known; wires that end beside it: 1'b0, Tx3, not_4_out, Rx1
  Pull_Resistor #(.pull(1)) pull_resistor_1 (.node(Rx1));

  assign Rx3 = Rx1;

  // Other names for the same wires on the sheet: Rx2 = Rx1
endmodule
